// Logisim project TP1_additions.circ as structural Verilog: 4 circuits, main circuit main
module main (
);


  // Notes on the sheet:
  //   VOIR CORRECTIONS DANS TP3_ARCHI (automate.circ)
endmodule

module Additionneur1bit (
  input  a,
  input  b,
  input  c_in,
  output S,
  output c_out
);

  wire and_1_out, and_2_out, and_3_out, or_1_out, xor_1_out;

  xor xor_1 (xor_1_out, a, b);
  and and_1 (and_1_out, a, b);
  and and_2 (and_2_out, a, c_in);
  and and_3 (and_3_out, c_in, b);
  or or_1 (or_1_out, and_1_out, and_2_out);
  xor xor_2 (S, xor_1_out, c_in);
  or or_2 (c_out, or_1_out, and_3_out);
endmodule

module Additionneur8bits (
  input  in_1,
  input  in_2,
  input  in_3,
  input  in_4,
  input  in_5,
  input  in_6,
  input  in_7,
  input  in_8,
  input  in_9,
  input  in_10,
  input  in_11,
  input  in_12,
  input  in_13,
  input  in_14,
  input  in_15,
  input  in_16,
  output out_17,
  output out_18,
  output out_19,
  output out_20,
  output out_21,
  output out_22,
  output out_23,
  output out_24
);

  wire additionneur1bit_1_c_out, additionneur1bit_2_c_out, additionneur1bit_3_c_out,
       additionneur1bit_4_c_out, additionneur1bit_5_c_out, additionneur1bit_6_c_out, additionneur1bit_7_c_out;

  Additionneur1bit additionneur1bit_1 (.a(in_1), .b(in_9), .c_in(1'b0), .S(out_17), .c_out(additionneur1bit_1_c_out));
  Additionneur1bit additionneur1bit_2 (
    .a(in_2), .b(in_10), .c_in(additionneur1bit_1_c_out), .S(out_18), .c_out(additionneur1bit_2_c_out));
  Additionneur1bit additionneur1bit_3 (
    .a(in_3), .b(in_11), .c_in(additionneur1bit_2_c_out), .S(out_19), .c_out(additionneur1bit_3_c_out));
  Additionneur1bit additionneur1bit_4 (
    .a(in_4), .b(in_12), .c_in(additionneur1bit_3_c_out), .S(out_20), .c_out(additionneur1bit_4_c_out));
  Additionneur1bit additionneur1bit_5 (
    .a(in_5), .b(in_13), .c_in(additionneur1bit_4_c_out), .S(out_21), .c_out(additionneur1bit_5_c_out));
  Additionneur1bit additionneur1bit_6 (
    .a(in_6), .b(in_14), .c_in(additionneur1bit_5_c_out), .S(out_22), .c_out(additionneur1bit_6_c_out));
  Additionneur1bit additionneur1bit_7 (
    .a(in_7), .b(in_15), .c_in(additionneur1bit_6_c_out), .S(out_23), .c_out(additionneur1bit_7_c_out));
  Additionneur1bit additionneur1bit_8 (
    .a(in_8), .b(in_16), .c_in(additionneur1bit_7_c_out), .S(out_24));  // open: c_out
endmodule

module AdditionneurSoustracteur8bits (
  input  Add_sub,
  input  [7:0] in_2,
  input  [7:0] in_3,
  output [7:0] out_4
);

  wire additionneur1bit_1_c_out, additionneur1bit_2_c_out, additionneur1bit_3_c_out,
       additionneur1bit_4_c_out, additionneur1bit_5_c_out, additionneur1bit_6_c_out,
       additionneur1bit_7_c_out, xor_1_out, xor_2_out, xor_3_out, xor_4_out, xor_5_out, xor_6_out, xor_7_out,
       xor_8_out;

  xor xor_1 (xor_1_out, in_2[7], Add_sub);
  Additionneur1bit additionneur1bit_1 (
    .a(in_3[7]), .b(xor_1_out), .c_in(Add_sub), .S(out_4[7]), .c_out(additionneur1bit_1_c_out));
  xor xor_2 (xor_2_out, in_2[6], Add_sub);
  Additionneur1bit additionneur1bit_2 (
    .a(in_3[6]), .b(xor_2_out), .c_in(additionneur1bit_1_c_out), .S(out_4[6]),
    .c_out(additionneur1bit_2_c_out));
  xor xor_3 (xor_3_out, in_2[5], Add_sub);
  Additionneur1bit additionneur1bit_3 (
    .a(in_3[5]), .b(xor_3_out), .c_in(additionneur1bit_2_c_out), .S(out_4[5]),
    .c_out(additionneur1bit_3_c_out));
  xor xor_4 (xor_4_out, in_2[4], Add_sub);
  Additionneur1bit additionneur1bit_4 (
    .a(in_3[4]), .b(xor_4_out), .c_in(additionneur1bit_3_c_out), .S(out_4[4]),
    .c_out(additionneur1bit_4_c_out));
  xor xor_5 (xor_5_out, in_2[3], Add_sub);
  Additionneur1bit additionneur1bit_5 (
    .a(in_3[3]), .b(xor_5_out), .c_in(additionneur1bit_4_c_out), .S(out_4[3]),
    .c_out(additionneur1bit_5_c_out));
  xor xor_6 (xor_6_out, in_2[2], Add_sub);
  Additionneur1bit additionneur1bit_6 (
    .a(in_3[2]), .b(xor_6_out), .c_in(additionneur1bit_5_c_out), .S(out_4[2]),
    .c_out(additionneur1bit_6_c_out));
  xor xor_7 (xor_7_out, in_2[1], Add_sub);
  Additionneur1bit additionneur1bit_7 (
    .a(in_3[1]), .b(xor_7_out), .c_in(additionneur1bit_6_c_out), .S(out_4[1]),
    .c_out(additionneur1bit_7_c_out));
  xor xor_8 (xor_8_out, in_2[0], Add_sub);
  Additionneur1bit additionneur1bit_8 (
    .a(in_3[0]), .b(xor_8_out), .c_in(additionneur1bit_7_c_out), .S(out_4[0]));  // open: c_out
endmodule
