// Logisim project TP1_memoire.circ as structural Verilog: 13 circuits, main circuit main
module main (
);


  // Notes on the sheet:
  //   VOIR CORRECTIONS DANS LE TP3_ARCHI
endmodule

module latch (
  input  D,
  input  Keep,
  output Q
);

  Multiplexer #(.enable("false")) multiplexer_1 (.in0(Q), .in1(D), .out(Q), .sel(Keep));
endmodule

module flip_flop (
  input  in_1,
  input  in_2,
  output out_3
);

  wire multiplexer_1_out;

  Multiplexer #(.enable("false")) multiplexer_1 (
    .in0(multiplexer_1_out), .in1(in_1), .out(multiplexer_1_out), .sel(in_2));
  Multiplexer #(.enable("false")) multiplexer_2 (.in0(multiplexer_1_out), .in1(out_3), .out(out_3), .sel(in_2));
endmodule

module flip_flop_resetable (
  input  e,
  input  reset,
  input  Clk,
  output q
);

  wire and_1_out, not_1_out;

  not not_1 (not_1_out, reset);
  and and_1 (and_1_out, e, not_1_out);
  flip_flop flip_flop_1 (.in_1(and_1_out), .out_3(q), .in_2(Clk));
endmodule

module flip_flop_enablable (
  input  in_1,
  input  in_2,
  input  in_3,
  input  in_4,
  output out_5
);

  wire multiplexer_1_out;

  flip_flop_resetable flip_flop_resetable_1 (.e(in_1), .reset(in_2), .q(out_5), .Clk(multiplexer_1_out));
  Multiplexer #(.enable("false")) multiplexer_1 (
    .in0(multiplexer_1_out), .in1(in_4), .out(multiplexer_1_out), .sel(in_3));
endmodule

module register (
  input  [7:0] In,
  input  Enable,
  input  Reset,
  input  Clk,
  output [7:0] Out
);

  flip_flop_enablable flip_flop_enablable_1 (.in_1(In[7]), .in_2(Reset), .in_3(Enable), .out_5(Out[7]), .in_4(Clk));
  flip_flop_enablable flip_flop_enablable_2 (.in_1(In[6]), .in_2(Reset), .in_3(Enable), .out_5(Out[6]), .in_4(Clk));
  flip_flop_enablable flip_flop_enablable_3 (.in_1(In[5]), .in_2(Reset), .in_3(Enable), .out_5(Out[5]), .in_4(Clk));
  flip_flop_enablable flip_flop_enablable_4 (.in_1(In[4]), .in_2(Reset), .in_3(Enable), .out_5(Out[4]), .in_4(Clk));
  flip_flop_enablable flip_flop_enablable_5 (.in_1(In[3]), .in_2(Reset), .in_3(Enable), .out_5(Out[3]), .in_4(Clk));
  flip_flop_enablable flip_flop_enablable_6 (.in_1(In[2]), .in_2(Reset), .in_3(Enable), .out_5(Out[2]), .in_4(Clk));
  flip_flop_enablable flip_flop_enablable_7 (.in_1(In[1]), .in_2(Reset), .in_3(Enable), .out_5(Out[1]), .in_4(Clk));
  flip_flop_enablable flip_flop_enablable_8 (.in_1(In[0]), .in_2(Reset), .in_3(Enable), .out_5(Out[0]), .in_4(Clk));
endmodule

module RAM_test (
  input  [7:0] Store_data,
  input  Store,
  input  [2:0] Address,
  input  Clk,
  output [7:0] out_5
);

  wire not_1_out;

  assign out_5 = Store ? Store_data : 8'bz;  // Controlled_Buffer controlled_buffer_1
  not not_1 (not_1_out, Store);
  RAM #(.addrWidth(3)) ram_1 (.addr(Address), .data(out_5), .clk(Clk), .ld(not_1_out));  // open: sel, clr
endmodule

module multiplexer (
  input  [2:0] Address,
  input  in_2,
  input  in_3,
  input  in_4,
  input  in_5,
  input  in_6,
  input  in_7,
  input  in_8,
  input  in_9,
  output s
);

  wire and_1_out, and_2_out, and_3_out, and_4_out, and_5_out, and_6_out, and_7_out, and_8_out, not_1_out,
       not_2_out, not_3_out;

  not not_1 (not_1_out, Address[1]);
  not not_2 (not_2_out, Address[2]);
  not not_3 (not_3_out, Address[0]);
  and and_1 (and_1_out, not_3_out, not_1_out, not_2_out, in_2);
  and and_2 (and_2_out, Address[0], not_1_out, not_2_out, in_3);
  and and_3 (and_3_out, not_3_out, Address[0], not_2_out, in_4);
  and and_4 (and_4_out, Address[1], Address[0], not_2_out, in_5);
  and and_5 (and_5_out, not_3_out, not_1_out, Address[2], in_6);
  and and_6 (and_6_out, Address[0], not_1_out, Address[2], in_7);
  and and_7 (and_7_out, not_3_out, Address[1], Address[2], in_8);
  and and_8 (and_8_out, Address[0], Address[1], Address[2], in_9);
  or or_1 (s, and_1_out, and_2_out, and_3_out, and_4_out, and_5_out, and_6_out, and_7_out, and_8_out);
endmodule

// DEMUX
module demultiplexer (
  input  [2:0] Address,
  input  e,
  output out_3,
  output out_4,
  output out_5,
  output out_6,
  output out_7,
  output out_8,
  output out_9,
  output out_10
);

  wire not_1_out, not_2_out, not_3_out;

  not not_1 (not_1_out, Address[2]);
  not not_2 (not_2_out, Address[1]);
  not not_3 (not_3_out, Address[0]);
  and and_1 (out_3, not_3_out, not_2_out, not_1_out, e);
  and and_2 (out_4, Address[0], not_2_out, not_1_out, e);
  and and_3 (out_5, not_3_out, Address[0], not_1_out, e);
  and and_4 (out_6, Address[1], Address[0], not_1_out, e);
  and and_5 (out_7, not_3_out, not_2_out, Address[2], e);
  and and_6 (out_8, Address[0], not_2_out, Address[2], e);
  and and_7 (out_9, not_3_out, Address[1], Address[2], e);
  and and_8 (out_10, Address[0], Address[1], Address[2], e);
endmodule

module multiplexer2 (
  input  [1:0] in_1,
  input  [1:0] in_2,
  input  [1:0] in_3,
  input  [1:0] in_4,
  input  [1:0] in_5,
  input  [1:0] in_6,
  input  [1:0] in_7,
  input  [1:0] in_8,
  input  [2:0] Address,
  output [1:0] out_10
);

  multiplexer multiplexer_1 (
    .in_2(in_8[0]), .in_3(in_7[0]), .in_4(in_6[0]), .in_5(in_5[0]), .in_6(in_4[0]), .in_7(in_3[0]),
    .in_8(in_2[0]), .in_9(in_1[0]), .s(out_10[0]), .Address(Address));
  multiplexer multiplexer_2 (
    .in_2(in_1[1]), .in_3(in_2[1]), .in_4(in_3[1]), .in_5(in_4[1]), .in_6(in_5[1]), .in_7(in_6[1]),
    .in_8(in_7[1]), .in_9(in_8[1]), .s(out_10[1]), .Address(Address));
endmodule

module multiplexer4 (
  input  [3:0] in_1,
  input  [3:0] in_2,
  input  [3:0] in_3,
  input  [3:0] in_4,
  input  [3:0] in_5,
  input  [3:0] in_6,
  input  [3:0] in_7,
  input  [3:0] in_8,
  input  [2:0] Address,
  output [3:0] out_10
);

  multiplexer2 multiplexer2_1 (
    .out_10(out_10[1:0]), .in_1(in_8[1:0]), .in_2(in_7[1:0]), .in_3(in_6[1:0]), .in_4(in_5[1:0]),
    .in_5(in_4[1:0]), .in_6(in_3[1:0]), .in_7(in_2[1:0]), .in_8(in_1[1:0]), .Address(Address));
  multiplexer2 multiplexer2_2 (
    .out_10(out_10[3:2]), .in_1(in_1[3:2]), .in_2(in_2[3:2]), .in_3(in_3[3:2]), .in_4(in_4[3:2]),
    .in_5(in_5[3:2]), .in_6(in_6[3:2]), .in_7(in_7[3:2]), .in_8(in_8[3:2]), .Address(Address));
endmodule

// MUX-8
module multiplexer8 (
  input  [7:0] in_1,
  input  [7:0] in_2,
  input  [7:0] in_3,
  input  [7:0] in_4,
  input  [7:0] in_5,
  input  [7:0] in_6,
  input  [7:0] in_7,
  input  [7:0] in_8,
  input  [2:0] Address,
  output [7:0] out_10
);

  multiplexer4 multiplexer4_1 (
    .out_10(out_10[3:0]), .in_1(in_8[3:0]), .in_2(in_7[3:0]), .in_3(in_6[3:0]), .in_4(in_5[3:0]),
    .in_5(in_4[3:0]), .in_6(in_3[3:0]), .in_7(in_2[3:0]), .in_8(in_1[3:0]), .Address(Address));
  multiplexer4 multiplexer4_2 (
    .out_10(out_10[7:4]), .in_1(in_1[7:4]), .in_2(in_2[7:4]), .in_3(in_3[7:4]), .in_4(in_4[7:4]),
    .in_5(in_5[7:4]), .in_6(in_6[7:4]), .in_7(in_7[7:4]), .in_8(in_8[7:4]), .Address(Address));
endmodule

module memoire (
  input  [2:0] Address,
  input  [7:0] D1,
  input  WE,
  output [7:0] W
);

  wire clock_1_out, demultiplexer_1_out_3, demultiplexer_1_out_4, demultiplexer_1_out_5,
       demultiplexer_1_out_6, demultiplexer_1_out_7, demultiplexer_1_out_8, demultiplexer_1_out_9,
       demultiplexer_1_out_10;
  wire [7:0] register_1_out, register_2_out, register_3_out, register_4_out, register_5_out, register_6_out,
       register_7_out, register_8_out;

  demultiplexer demultiplexer_1 (
    .e(WE), .out_3(demultiplexer_1_out_3), .out_4(demultiplexer_1_out_4), .out_5(demultiplexer_1_out_5),
    .out_6(demultiplexer_1_out_6), .out_7(demultiplexer_1_out_7), .out_8(demultiplexer_1_out_8),
    .out_9(demultiplexer_1_out_9), .out_10(demultiplexer_1_out_10), .Address(Address));
  register register_1 (
    .In(D1), .Out(register_1_out), .Reset(demultiplexer_1_out_3), .Clk(clock_1_out));  // open: Enable
  register register_2 (
    .In(D1), .Out(register_2_out), .Reset(demultiplexer_1_out_4), .Clk(clock_1_out));  // open: Enable
  register register_3 (
    .In(D1), .Out(register_3_out), .Reset(demultiplexer_1_out_5), .Clk(clock_1_out));  // open: Enable
  register register_4 (
    .In(D1), .Out(register_4_out), .Reset(demultiplexer_1_out_6), .Clk(clock_1_out));  // open: Enable
  register register_5 (
    .In(D1), .Out(register_5_out), .Reset(demultiplexer_1_out_7), .Clk(clock_1_out));  // open: Enable
  register register_6 (
    .In(D1), .Out(register_6_out), .Reset(demultiplexer_1_out_8), .Clk(clock_1_out));  // open: Enable
  register register_7 (
    .In(D1), .Out(register_7_out), .Reset(demultiplexer_1_out_9), .Clk(clock_1_out));  // open: Enable
  register register_8 (
    .In(D1), .Out(register_8_out), .Reset(demultiplexer_1_out_10), .Clk(clock_1_out));  // open: Enable
  Clock clock_1 (.out(clock_1_out));
  multiplexer8 multiplexer8_1 (
    .out_10(W), .in_1(register_1_out), .in_2(register_2_out), .in_3(register_3_out), .in_4(register_4_out),
    .in_5(register_5_out), .in_6(register_6_out), .in_7(register_7_out), .in_8(register_8_out),
    .Address(Address));
endmodule
