// Logisim project division.circ as structural Verilog: 10 circuits, main circuit main
module main (
  input  Reset,
  input  go,
  input  [7:0] N,
  input  [7:0] P,
  output Ok,
  output [7:0] Q
);

  wire Clk_out, LN, LP, LQ, LX, n8bitscompare_1_out_3, RQ, RX;
  wire [7:0] n8bitsadder_1_out_3, n8bitsadder_2_out_3, n8bitsregister_1_out, n8bitsregister_2_out,
       n8bitsregister_3_out;

  Clock Clk (.out(Clk_out));
  _8bitsRegister u_8bitsregister_1 (.In(N), .Out(n8bitsregister_1_out), .Enable(LN), .Reset(Reset), .Clk(Clk_out));
  _8bitsRegister u_8bitsregister_2 (
    .In(n8bitsadder_1_out_3), .Out(n8bitsregister_2_out), .Enable(LX), .Reset(RX), .Clk(Clk_out));
  _8bitsRegister u_8bitsregister_3 (.In(P), .Out(n8bitsregister_3_out), .Enable(LP), .Reset(Reset), .Clk(Clk_out));
  _8bitsRegister u_8bitsregister_4 (.In(n8bitsadder_2_out_3), .Out(Q), .Enable(LQ), .Reset(RQ), .Clk(Clk_out));
  // Probe on n8bitsregister_1_out
  // Probe on n8bitsregister_2_out
  // Probe on n8bitsregister_3_out
  _8bitsAdder u_8bitsadder_1 (.in_1(n8bitsregister_2_out), .in_2(n8bitsregister_3_out), .out_3(n8bitsadder_1_out_3));
  _8bitsAdder u_8bitsadder_2 (.in_1(Q), .in_2(8'h1), .out_3(n8bitsadder_2_out_3));
  Controller Controller (
    .Enable(1'b1), .Reset(Reset), .go(go), .pp(n8bitscompare_1_out_3), .clk(Clk_out), .RQ(RQ), .LQ(LQ),
    .LP(LP), .RX(RX), .LX(LX), .LN(LN), .Ok(Ok));
  _8bitsCompare u_8bitscompare_1 (.A(n8bitsadder_1_out_3), .B(n8bitsregister_1_out), .out_3(n8bitscompare_1_out_3));

  // Notes on the sheet:
  //   déterminé (pas de rouge) et mettre 'Reset' à 0.
  //   Pour démarer le diviseur, mettre 'Reset' à 1, puis démarer 
  //   l'horloge (ticks enabled), attendre que tout ait un état
endmodule

module T (
  input  go,
  input  pp,
  input  [1:0] q,
  output [1:0] out_4
);

  wire and_1_out, and_2_out, and_3_out, not_1_out, not_2_out, xor_1_out, xor_2_out, xor_3_out;

  and and_1 (and_1_out, go, q[1]);
  xor xor_1 (xor_1_out, q[1], q[0]);
  not not_1 (not_1_out, xor_1_out);
  xor xor_2 (xor_2_out, q[1], q[0]);
  not not_2 (not_2_out, pp);
  xor xor_3 (xor_3_out, q[0], q[1]);
  and and_2 (and_2_out, not_1_out, go);
  and and_3 (and_3_out, xor_2_out, not_2_out);
  or or_1 (out_4[1], xor_3_out, and_1_out);
  or or_2 (out_4[0], and_2_out, and_3_out);
endmodule

module S (
  input  [1:0] in_1,
  output [6:0] out_2
);

  wire not_1_out, or_1_out, xor_1_out;

  not not_1 (not_1_out, in_1[1]);
  not not_2 (out_2[2], in_1[0]);
  or or_1 (or_1_out, in_1[0], in_1[1]);
  or or_2 (out_2[5], not_1_out, out_2[2]);
  xor xor_1 (xor_1_out, in_1[0], in_1[1]);
  and and_1 (out_2[0], in_1[0], in_1[1]);
  not not_3 (out_2[6], or_1_out);
  not not_4 (out_2[4], xor_1_out);

  assign {out_2[3], out_2[1]} = {2{out_2[4]}};
endmodule

module Controller (
  input  Enable,
  input  Reset,
  input  go,
  input  pp,
  input  clk,
  output Ok,
  output RQ,
  output LQ,
  output LP,
  output RX,
  output LX,
  output LN
);

  wire [1:0] n2bitsregister_1_out, t_1_out_4;

  T t_1 (.go(go), .pp(pp), .q(n2bitsregister_1_out), .out_4(t_1_out_4));
  _2bitsRegister u_2bitsregister_1 (
    .In(t_1_out_4), .Out(n2bitsregister_1_out), .Enable(Enable), .Reset(Reset), .Clk(clk));
  // Probe on n2bitsregister_1_out
  // Probe on {LN, LX, RX, LP, LQ, RQ, Ok}
  S s_1 (.in_1(n2bitsregister_1_out), .out_2({LN, LX, RX, LP, LQ, RQ, Ok}));

  // Notes on the sheet:
  //   Reset: pull=down
  //   Enable: pull=up
endmodule

module _2bitsRegister (
  input  [1:0] In,
  input  Enable,
  input  Reset,
  input  Clk,
  output [1:0] Out
);

  flip_flop_enablable flip_flop_enablable_1 (.in_1(In[1]), .in_2(Reset), .in_3(Enable), .out_5(Out[1]), .in_4(Clk));
  flip_flop_enablable flip_flop_enablable_2 (.in_1(In[0]), .in_2(Reset), .in_3(Enable), .out_5(Out[0]), .in_4(Clk));
endmodule

module _8bitsAdder (
  input  [7:0] in_1,
  input  [7:0] in_2,
  output [7:0] out_3
);

  wire additionneur1bit_1_c_out, additionneur1bit_2_c_out, additionneur1bit_3_c_out,
       additionneur1bit_4_c_out, additionneur1bit_5_c_out, additionneur1bit_6_c_out, additionneur1bit_7_c_out;

  Additionneur1bit additionneur1bit_1 (
    .a(in_1[0]), .b(in_2[0]), .c_in(1'b0), .S(out_3[0]), .c_out(additionneur1bit_1_c_out));
  Additionneur1bit additionneur1bit_2 (
    .a(in_1[1]), .b(in_2[1]), .c_in(additionneur1bit_1_c_out), .S(out_3[1]), .c_out(additionneur1bit_2_c_out));
  Additionneur1bit additionneur1bit_3 (
    .a(in_1[2]), .b(in_2[2]), .c_in(additionneur1bit_2_c_out), .S(out_3[2]), .c_out(additionneur1bit_3_c_out));
  Additionneur1bit additionneur1bit_4 (
    .a(in_1[3]), .b(in_2[3]), .c_in(additionneur1bit_3_c_out), .S(out_3[3]), .c_out(additionneur1bit_4_c_out));
  Additionneur1bit additionneur1bit_5 (
    .a(in_1[4]), .b(in_2[4]), .c_in(additionneur1bit_4_c_out), .S(out_3[4]), .c_out(additionneur1bit_5_c_out));
  Additionneur1bit additionneur1bit_6 (
    .a(in_1[5]), .b(in_2[5]), .c_in(additionneur1bit_5_c_out), .S(out_3[5]), .c_out(additionneur1bit_6_c_out));
  Additionneur1bit additionneur1bit_7 (
    .a(in_1[6]), .b(in_2[6]), .c_in(additionneur1bit_6_c_out), .S(out_3[6]), .c_out(additionneur1bit_7_c_out));
  Additionneur1bit additionneur1bit_8 (
    .a(in_1[7]), .b(in_2[7]), .c_in(additionneur1bit_7_c_out), .S(out_3[7]));  // open: c_out
endmodule

module _8bitsSubstracter (
  input  [7:0] in_1,
  input  [7:0] in_2,
  output [7:0] out_3
);

  wire [7:0] n8bitsadder_1_out_3, not_1_out;

  assign not_1_out = ~in_2;  // NOT_Gate not_1, 8 bits wide
  _8bitsAdder u_8bitsadder_1 (.in_1(not_1_out), .in_2(8'h1), .out_3(n8bitsadder_1_out_3));
  _8bitsAdder u_8bitsadder_2 (.in_1(in_1), .in_2(n8bitsadder_1_out_3), .out_3(out_3));
endmodule

module _8bitsCompare (
  input  [7:0] A,
  input  [7:0] B,
  output out_3
);

  wire and_1_out;
  wire [6:0] not_1_out;
  wire [7:0] n8bitssubstracter_1_out_3;

  _8bitsSubstracter u_8bitssubstracter_1 (.in_1(A), .in_2(B), .out_3(n8bitssubstracter_1_out_3));
  assign not_1_out = ~n8bitssubstracter_1_out_3[6:0];  // NOT_Gate not_1, 7 bits wide
  and and_1 (and_1_out, not_1_out[0], not_1_out[1], not_1_out[2], not_1_out[3], not_1_out[4], not_1_out[5], not_1_out[6]);
  or or_1 (out_3, and_1_out, n8bitssubstracter_1_out_3[7]);

  // Notes on the sheet:
  //   A <= B
endmodule

module AddSoustract (
  input  Add_sub,
  input  [7:0] in_2,
  input  [7:0] in_3,
  output [7:0] out_4
);

  wire additionneur1bit_1_c_out, additionneur1bit_2_c_out, additionneur1bit_3_c_out,
       additionneur1bit_4_c_out, additionneur1bit_5_c_out, additionneur1bit_6_c_out,
       additionneur1bit_7_c_out, xor_1_out, xor_2_out, xor_3_out, xor_4_out, xor_5_out, xor_6_out, xor_7_out,
       xor_8_out;

  xor xor_1 (xor_1_out, in_2[7], Add_sub);
  Additionneur1bit additionneur1bit_1 (
    .a(in_3[7]), .b(xor_1_out), .c_in(Add_sub), .S(out_4[7]), .c_out(additionneur1bit_1_c_out));
  xor xor_2 (xor_2_out, in_2[6], Add_sub);
  Additionneur1bit additionneur1bit_2 (
    .a(in_3[6]), .b(xor_2_out), .c_in(additionneur1bit_1_c_out), .S(out_4[6]),
    .c_out(additionneur1bit_2_c_out));
  xor xor_3 (xor_3_out, in_2[5], Add_sub);
  Additionneur1bit additionneur1bit_3 (
    .a(in_3[5]), .b(xor_3_out), .c_in(additionneur1bit_2_c_out), .S(out_4[5]),
    .c_out(additionneur1bit_3_c_out));
  xor xor_4 (xor_4_out, in_2[4], Add_sub);
  Additionneur1bit additionneur1bit_4 (
    .a(in_3[4]), .b(xor_4_out), .c_in(additionneur1bit_3_c_out), .S(out_4[4]),
    .c_out(additionneur1bit_4_c_out));
  xor xor_5 (xor_5_out, in_2[3], Add_sub);
  Additionneur1bit additionneur1bit_5 (
    .a(in_3[3]), .b(xor_5_out), .c_in(additionneur1bit_4_c_out), .S(out_4[3]),
    .c_out(additionneur1bit_5_c_out));
  xor xor_6 (xor_6_out, in_2[2], Add_sub);
  Additionneur1bit additionneur1bit_6 (
    .a(in_3[2]), .b(xor_6_out), .c_in(additionneur1bit_5_c_out), .S(out_4[2]),
    .c_out(additionneur1bit_6_c_out));
  xor xor_7 (xor_7_out, in_2[1], Add_sub);
  Additionneur1bit additionneur1bit_7 (
    .a(in_3[1]), .b(xor_7_out), .c_in(additionneur1bit_6_c_out), .S(out_4[1]),
    .c_out(additionneur1bit_7_c_out));
  xor xor_8 (xor_8_out, in_2[0], Add_sub);
  Additionneur1bit additionneur1bit_8 (
    .a(in_3[0]), .b(xor_8_out), .c_in(additionneur1bit_7_c_out), .S(out_4[0]));  // open: c_out
endmodule

module _8bitsRegister (
  input  [7:0] In,
  input  Enable,
  input  Reset,
  input  Clk,
  output [7:0] Out
);

  flip_flop_enablable flip_flop_enablable_1 (.in_1(In[7]), .in_2(Reset), .in_3(Enable), .out_5(Out[7]), .in_4(Clk));
  flip_flop_enablable flip_flop_enablable_2 (.in_1(In[6]), .in_2(Reset), .in_3(Enable), .out_5(Out[6]), .in_4(Clk));
  flip_flop_enablable flip_flop_enablable_3 (.in_1(In[5]), .in_2(Reset), .in_3(Enable), .out_5(Out[5]), .in_4(Clk));
  flip_flop_enablable flip_flop_enablable_4 (.in_1(In[4]), .in_2(Reset), .in_3(Enable), .out_5(Out[4]), .in_4(Clk));
  flip_flop_enablable flip_flop_enablable_5 (.in_1(In[3]), .in_2(Reset), .in_3(Enable), .out_5(Out[3]), .in_4(Clk));
  flip_flop_enablable flip_flop_enablable_6 (.in_1(In[2]), .in_2(Reset), .in_3(Enable), .out_5(Out[2]), .in_4(Clk));
  flip_flop_enablable flip_flop_enablable_7 (.in_1(In[1]), .in_2(Reset), .in_3(Enable), .out_5(Out[1]), .in_4(Clk));
  flip_flop_enablable flip_flop_enablable_8 (.in_1(In[0]), .in_2(Reset), .in_3(Enable), .out_5(Out[0]), .in_4(Clk));
endmodule
